// Digital circuit test_circuit.dig as structural Verilog
module test_circuit (
  input  Clock,
  input  load_enable,
  input  [4:0] reg_sel,
  input  Reset,
  output Hazard_Stall,
  output Hazard_Flush,
  output [31:0] Stage_EX_PC,
  output [31:0] Stage_ID_PC,
  output [31:0] Stage_IF_PC,
  output [31:0] Reg_Debug,
  output [31:0] ALU_Result,
  output [31:0] Instr_Debug,
  output [31:0] PC_Debug
);

  wire u_riscv_cpu_dmem_we_o;
  wire [31:0] ramdualport_1_d, ROM_d, u_riscv_cpu_dmem_addr_o, u_riscv_cpu_dmem_wdata_o,
       u_riscv_cpu_imem_addr_o;

  riscv_cpu #(.applicationType("IVERILOG"), .CodeFile("/home/matsilva/desktop/Prog/EEL580/EEL580-CPU-RISCV/riscv_cpu_all.v")) u_riscv_cpu (
    .clk_i(Clock), .reset_i(Reset), .load_enable_i(Reset), .imem_data_i(ROM_d),
    .dmem_rdata_i(ramdualport_1_d), .reg_sel_i(reg_sel), .imem_addr_o(u_riscv_cpu_imem_addr_o),
    .dmem_addr_o(u_riscv_cpu_dmem_addr_o), .dmem_wdata_o(u_riscv_cpu_dmem_wdata_o),
    .dmem_we_o(u_riscv_cpu_dmem_we_o), .pc_debug_o(PC_Debug), .instr_debug_o(Instr_Debug),
    .alu_result_debug_o(ALU_Result), .reg_debug_o(Reg_Debug), .stage_if_pc_o(Stage_IF_PC),
    .stage_id_pc_o(Stage_ID_PC), .stage_ex_pc_o(Stage_EX_PC), .hazard_stall_o(Hazard_Stall),
    .hazard_flush_o(Hazard_Flush));
  ROM #(.AddrBits(8), .Bits(32)) ROM (.A(u_riscv_cpu_imem_addr_o[9:2]), .sel(load_enable), .D(ROM_d));
  RAMDualPort #(.AddrBits(8), .Bits(32)) ramdualport_1 (
    .A(u_riscv_cpu_dmem_addr_o[9:2]), .Din(u_riscv_cpu_dmem_wdata_o), .str(u_riscv_cpu_dmem_we_o), .C(Clock),
    .ld(load_enable), .D(ramdualport_1_d));

  // Notes on the sheet:
  //   contents of ROM (hex, n*v repeats v):
  //   500093,300113,2081b3,40208233,20f2b3,20e333,20c3b3,10f413,80e493
  //   ,50c513,1000593,259613,25d693,259733,25d7b3,6400813,1002023,2883
  //   ,12345937,997,318463,6300a13,700a13,109463,2a00a93,209463,5800b13
  //   ,b00b13,800bef,3700c13,4d00c13,c93,c97,10c8c93,c8d67,4200d93,2100d93
  //   ,a00e13,5e0e13,3e0e13,c800e93,1d02223,402f03,1f0fb3,5*13
endmodule
